// Logisim project GrayCodeGeneratorUndDecoder.circ as structural Verilog: 5 circuits, main circuit main
module main (
  input  Enable,
  input  Reset,
  output A,
  output B,
  output S1,
  output C,
  output S2,
  output D,
  output S3,
  output Enable_2,
  output S4,
  output Z1,
  output Z2,
  output Z3,
  output Z4
);

  wire clock_1_out, erste7siegment_1_a1, erste7siegment_1_b1, erste7siegment_1_c1, erste7siegment_1_d1,
       erste7siegment_1_e1, erste7siegment_1_f1, erste7siegment_1_g1, erste7siegment_2_a1,
       erste7siegment_2_b1, erste7siegment_2_c1, erste7siegment_2_d1, erste7siegment_2_e1,
       erste7siegment_2_f1, erste7siegment_2_g1, n3bitscounter_1_a, n3bitscounter_1_b, n3bitscounter_1_c,
       n3bitscounter_1_d, zweite7segment_1_a2, zweite7segment_1_b2, zweite7segment_1_c2, zweite7segment_1_d2,
       zweite7segment_1_e2, zweite7segment_1_f2, zweite7segment_1_g2, zweite7segment_2_a2,
       zweite7segment_2_b2, zweite7segment_2_c2, zweite7segment_2_d2, zweite7segment_2_e2,
       zweite7segment_2_f2, zweite7segment_2_g2;

  Clock clock_1 (.out(clock_1_out));
  _3BitsCounter u_3bitscounter_1 (
    .Enable(Enable), .CLK(clock_1_out), .Rest(Reset), .A(n3bitscounter_1_a), .B(n3bitscounter_1_b),
    .C(n3bitscounter_1_c), .D(n3bitscounter_1_d), .Enable_2(Enable_2));
  Erste7Siegment erste7siegment_1 (
    .Enable(Enable_2), .D(n3bitscounter_1_d), .C(n3bitscounter_1_c), .B(n3bitscounter_1_b),
    .A(n3bitscounter_1_a), .a1(erste7siegment_1_a1), .b1(erste7siegment_1_b1), .c1(erste7siegment_1_c1),
    .d1(erste7siegment_1_d1), .e1(erste7siegment_1_e1), .f1(erste7siegment_1_f1), .g1(erste7siegment_1_g1));
  Zweite7Segment zweite7segment_1 (
    .Enable(Enable_2), .D(n3bitscounter_1_d), .C(n3bitscounter_1_c), .B(n3bitscounter_1_b),
    .A(n3bitscounter_1_a), .a2(zweite7segment_1_a2), .b2(zweite7segment_1_b2), .c2(zweite7segment_1_c2),
    .d2(zweite7segment_1_d2), .e2(zweite7segment_1_e2), .f2(zweite7segment_1_f2), .g2(zweite7segment_1_g2));
  _7_Segment_Display u_7_segment_display_1 (
    .g(zweite7segment_1_g2), .f(zweite7segment_1_f2), .a(zweite7segment_1_a2), .b(zweite7segment_1_b2),
    .e(zweite7segment_1_e2), .d(zweite7segment_1_d2), .c(zweite7segment_1_c2));  // open: dp
  _7_Segment_Display u_7_segment_display_2 (
    .g(erste7siegment_1_g1), .f(erste7siegment_1_f1), .a(erste7siegment_1_a1), .b(erste7siegment_1_b1),
    .e(erste7siegment_1_e1), .d(erste7siegment_1_d1), .c(erste7siegment_1_c1));  // open: dp
  xor XOR (A, n3bitscounter_1_a, n3bitscounter_1_b);
  xor XOR_2 (B, n3bitscounter_1_b, n3bitscounter_1_c);
  xor XOR_3 (C, n3bitscounter_1_c, n3bitscounter_1_d);
  xor XOR_4 (D, n3bitscounter_1_d, Enable_2);
  Erste7Siegment erste7siegment_2 (
    .Enable(Enable_2), .D(D), .C(C), .B(B), .A(A), .a1(erste7siegment_2_a1), .b1(erste7siegment_2_b1),
    .c1(erste7siegment_2_c1), .d1(erste7siegment_2_d1), .e1(erste7siegment_2_e1), .f1(erste7siegment_2_f1),
    .g1(erste7siegment_2_g1));
  Zweite7Segment zweite7segment_2 (
    .Enable(Enable_2), .D(D), .C(C), .B(B), .A(A), .a2(zweite7segment_2_a2), .b2(zweite7segment_2_b2),
    .c2(zweite7segment_2_c2), .d2(zweite7segment_2_d2), .e2(zweite7segment_2_e2), .f2(zweite7segment_2_f2),
    .g2(zweite7segment_2_g2));
  _7_Segment_Display u_7_segment_display_3 (
    .g(zweite7segment_2_g2), .f(zweite7segment_2_f2), .a(zweite7segment_2_a2), .b(zweite7segment_2_b2),
    .e(zweite7segment_2_e2), .d(zweite7segment_2_d2), .c(zweite7segment_2_c2));  // open: dp
  Decoder decoder_1 (
    .Enable(Enable_2), .D(D), .C(C), .B(B), .A(A), .S1(S1), .S2(S2), .S3(S3), .S4(S4), .Z1(Z1), .Z2(Z2),
    .Z3(Z3), .Z4(Z4));
  _7_Segment_Display u_7_segment_display_4 (
    .g(erste7siegment_2_g1), .f(erste7siegment_2_f1), .a(erste7siegment_2_a1), .b(erste7siegment_2_b1),
    .e(erste7siegment_2_e1), .d(erste7siegment_2_d1), .c(erste7siegment_2_c1));  // open: dp

  // Notes on the sheet:
  //   Takt
  //   Bänar Zähler
  //   von Bänar zum Gray Code
  //   Gray Code Zähler
  //   Decoder
endmodule

module _3BitsCounter (
  input  Enable,
  input  CLK,
  input  Rest,
  output A,
  output B,
  output C,
  output D,
  output Enable_2
);

  wire and_1_out, and_2_out, and_3_out, and_4_out, xor_1_out, xor_2_out, xor_3_out, xor_4_out, xor_5_out;

  and and_1 (and_1_out, Enable, A);
  and and_2 (and_2_out, and_1_out, B);
  and and_3 (and_3_out, and_2_out, C);
  and and_4 (and_4_out, and_3_out, D);
  xor xor_1 (xor_1_out, A, Enable);
  xor xor_2 (xor_2_out, B, and_1_out);
  xor xor_3 (xor_3_out, C, and_2_out);
  xor xor_4 (xor_4_out, D, and_3_out);
  xor xor_5 (xor_5_out, Enable_2, and_4_out);
  D_Flip_Flop d_ff_1 (.clk(CLK), .D(xor_1_out), .Q(A), .reset(Rest));  // open: Qn, preset, en
  D_Flip_Flop d_ff_2 (.clk(CLK), .D(xor_2_out), .Q(B), .reset(Rest));  // open: Qn, preset, en
  D_Flip_Flop d_ff_3 (.clk(CLK), .D(xor_3_out), .Q(C), .reset(Rest));  // open: Qn, preset, en
  D_Flip_Flop d_ff_4 (.clk(CLK), .D(xor_4_out), .Q(D), .reset(Rest));  // open: Qn, preset, en
  D_Flip_Flop d_ff_5 (.clk(CLK), .D(xor_5_out), .Q(Enable_2), .reset(Rest));  // open: Qn, preset, en
endmodule

// Erste / Segemet Ziffer
module Erste7Siegment (
  input  Enable,
  input  D,
  input  C,
  input  B,
  input  A,
  output a1,
  output b1,
  output c1,
  output d1,
  output e1,
  output f1,
  output g1
);

  wire and_1_out, and_2_out, and_3_out, and_4_out, and_5_out, and_6_out, and_7_out, and_8_out, and_9_out,
       and_10_out, and_11_out, and_12_out, and_13_out, and_14_out, and_15_out, and_16_out, and_17_out,
       and_18_out, and_19_out, and_20_out, and_21_out, and_22_out, and_23_out, and_24_out, and_25_out,
       and_26_out, and_27_out, and_28_out, and_29_out, and_30_out, and_31_out, and_32_out, and_33_out,
       and_34_out, and_35_out, and_36_out, and_37_out, and_38_out, and_39_out, and_40_out, and_41_out,
       and_42_out, and_43_out, and_44_out, and_45_out, and_46_out, and_47_out, and_48_out, and_49_out,
       and_50_out, and_51_out, and_52_out, and_53_out, and_54_out, and_55_out, and_56_out, and_57_out,
       and_58_out, and_59_out, and_60_out, and_61_out, and_62_out, and_63_out, and_64_out, and_65_out,
       and_66_out, and_67_out, and_68_out, and_69_out, and_70_out, and_71_out, and_72_out, and_73_out,
       and_74_out, and_75_out, and_76_out, and_77_out, and_78_out, and_79_out, and_80_out, and_81_out,
       and_82_out, and_83_out, and_84_out, and_85_out, and_86_out, and_87_out, and_88_out, and_89_out,
       and_90_out, and_91_out, and_92_out, and_93_out, and_94_out, and_95_out, and_96_out, and_97_out,
       and_98_out, and_99_out, and_100_out, and_101_out, and_102_out, and_103_out, and_104_out, and_105_out,
       and_106_out, and_107_out, not_1_out, not_2_out, not_3_out, not_4_out, not_5_out, not_6_out, not_7_out,
       not_8_out, not_9_out, not_10_out, not_11_out, not_12_out, not_13_out, not_14_out, not_15_out,
       not_16_out, not_17_out, not_18_out, not_19_out, not_20_out, not_21_out, not_22_out, not_23_out,
       not_24_out, not_25_out, not_26_out, not_27_out, not_28_out, not_29_out, not_30_out, not_31_out,
       not_32_out, not_33_out, not_34_out, not_35_out, not_36_out, not_37_out, not_38_out, not_39_out,
       not_40_out, not_41_out, not_42_out, not_43_out, not_44_out, not_45_out, not_46_out, not_47_out,
       not_48_out, not_49_out, not_50_out, not_51_out, not_52_out, not_53_out, not_54_out, not_55_out,
       not_56_out, not_57_out, not_58_out, not_59_out, not_60_out, not_61_out, not_62_out, not_63_out,
       not_64_out, not_65_out, not_66_out, not_67_out, not_68_out, not_69_out, not_70_out, not_71_out,
       not_72_out, not_73_out, not_74_out, not_75_out, not_76_out, not_77_out, not_78_out, not_79_out,
       not_80_out, not_81_out, not_82_out, not_83_out, not_84_out, not_85_out, or_1_out, or_2_out, or_3_out,
       or_4_out, or_5_out, or_6_out, or_7_out, or_8_out, or_9_out, or_10_out, or_11_out, or_12_out,
       or_13_out, or_14_out, or_15_out, or_16_out, or_17_out, or_18_out, or_19_out, or_20_out, or_21_out,
       or_22_out, or_23_out, or_24_out, or_25_out, or_26_out, or_27_out, or_28_out, or_29_out, or_30_out,
       or_31_out, or_32_out, or_33_out, or_34_out, or_35_out, or_36_out, or_38_out, or_39_out, or_41_out,
       or_42_out;

  not not_1 (not_1_out, C);
  not not_2 (not_2_out, Enable);
  not not_3 (not_3_out, Enable);
  not not_4 (not_4_out, D);
  not not_5 (not_5_out, C);
  not not_6 (not_6_out, D);
  not not_7 (not_7_out, C);
  not not_8 (not_8_out, D);
  not not_9 (not_9_out, C);
  not not_10 (not_10_out, Enable);
  not not_11 (not_11_out, Enable);
  not not_12 (not_12_out, Enable);
  not not_13 (not_13_out, D);
  not not_14 (not_14_out, D);
  not not_15 (not_15_out, C);
  not not_16 (not_16_out, D);
  not not_17 (not_17_out, C);
  not not_18 (not_18_out, B);
  not not_19 (not_19_out, Enable);
  not not_20 (not_20_out, D);
  not not_21 (not_21_out, C);
  not not_22 (not_22_out, Enable);
  not not_23 (not_23_out, D);
  not not_24 (not_24_out, B);
  not not_25 (not_25_out, Enable);
  not not_26 (not_26_out, D);
  not not_27 (not_27_out, A);
  not not_28 (not_28_out, C);
  not not_29 (not_29_out, Enable);
  not not_30 (not_30_out, B);
  not not_31 (not_31_out, D);
  not not_32 (not_32_out, C);
  not not_33 (not_33_out, D);
  not not_34 (not_34_out, C);
  not not_35 (not_35_out, D);
  not not_36 (not_36_out, Enable);
  not not_37 (not_37_out, Enable);
  not not_38 (not_38_out, C);
  not not_39 (not_39_out, D);
  and and_1 (and_1_out, not_1_out, B);
  not not_40 (not_40_out, A);
  and and_2 (and_2_out, not_2_out, C);
  and and_3 (and_3_out, not_3_out, D);
  not not_41 (not_41_out, B);
  and and_4 (and_4_out, D, C);
  not not_42 (not_42_out, B);
  and and_5 (and_5_out, Enable, not_4_out);
  not not_43 (not_43_out, C);
  and and_6 (and_6_out, Enable, not_5_out);
  and and_7 (and_7_out, Enable, C);
  not not_44 (not_44_out, A);
  and and_8 (and_8_out, not_6_out, not_7_out);
  and and_9 (and_9_out, not_8_out, not_9_out);
  not not_45 (not_45_out, D);
  not not_46 (not_46_out, C);
  not not_47 (not_47_out, B);
  and and_10 (and_10_out, not_10_out, D);
  not not_48 (not_48_out, C);
  and and_11 (and_11_out, not_11_out, D);
  not not_49 (not_49_out, B);
  not not_50 (not_50_out, Enable);
  not not_51 (not_51_out, B);
  and and_12 (and_12_out, not_12_out, not_13_out);
  not not_52 (not_52_out, C);
  and and_13 (and_13_out, not_14_out, not_15_out);
  and and_14 (and_14_out, not_16_out, B);
  not not_53 (not_53_out, A);
  not not_54 (not_54_out, C);
  not not_55 (not_55_out, Enable);
  not not_56 (not_56_out, B);
  not not_57 (not_57_out, Enable);
  and and_15 (and_15_out, D, not_17_out);
  and and_16 (and_16_out, not_18_out, A);
  and and_17 (and_17_out, not_19_out, D);
  and and_18 (and_18_out, C, A);
  not not_58 (not_58_out, D);
  not not_59 (not_59_out, D);
  and and_19 (and_19_out, not_20_out, B);
  not not_60 (not_60_out, A);
  and and_20 (and_20_out, not_21_out, B);
  not not_61 (not_61_out, A);
  not not_62 (not_62_out, Enable);
  not not_63 (not_63_out, B);
  not not_64 (not_64_out, A);
  not not_65 (not_65_out, D);
  and and_21 (and_21_out, not_22_out, not_23_out);
  and and_22 (and_22_out, C, not_24_out);
  and and_23 (and_23_out, not_25_out, not_26_out);
  and and_24 (and_24_out, C, not_27_out);
  and and_25 (and_25_out, D, not_28_out);
  not not_66 (not_66_out, B);
  and and_26 (and_26_out, D, B);
  not not_67 (not_67_out, A);
  and and_27 (and_27_out, not_29_out, D);
  and and_28 (and_28_out, C, B);
  and and_29 (and_29_out, Enable, not_30_out);
  not not_68 (not_68_out, A);
  and and_30 (and_30_out, Enable, not_31_out);
  and and_31 (and_31_out, not_32_out, B);
  and and_32 (and_32_out, Enable, D);
  not not_69 (not_69_out, B);
  and and_33 (and_33_out, not_33_out, not_34_out);
  and and_34 (and_34_out, not_35_out, B);
  not not_70 (not_70_out, A);
  and and_35 (and_35_out, not_36_out, C);
  not not_71 (not_71_out, B);
  not not_72 (not_72_out, B);
  and and_36 (and_36_out, not_37_out, D);
  and and_37 (and_37_out, Enable, not_38_out);
  not not_73 (not_73_out, A);
  not not_74 (not_74_out, D);
  and and_38 (and_38_out, not_39_out, B);
  or or_1 (or_1_out, and_38_out, and_39_out);
  and and_39 (and_39_out, and_1_out, not_40_out);
  and and_40 (and_40_out, and_2_out, A);
  or or_2 (or_2_out, and_40_out, and_41_out);
  and and_41 (and_41_out, and_3_out, not_41_out);
  and and_42 (and_42_out, and_4_out, not_42_out);
  or or_3 (or_3_out, and_42_out, and_43_out);
  and and_43 (and_43_out, and_5_out, not_43_out);
  and and_44 (and_44_out, and_6_out, A);
  or or_4 (or_4_out, and_44_out, and_45_out);
  and and_45 (and_45_out, and_7_out, not_44_out);
  and and_46 (and_46_out, and_8_out, A);
  or or_5 (or_5_out, and_46_out, and_47_out);
  and and_47 (and_47_out, and_9_out, B);
  and and_48 (and_48_out, not_45_out, B);
  and and_49 (and_49_out, and_48_out, A);
  and and_50 (and_50_out, not_46_out, B);
  and and_51 (and_51_out, and_50_out, A);
  and and_52 (and_52_out, C, not_47_out);
  and and_53 (and_53_out, and_52_out, not_75_out);
  not not_75 (not_75_out, A);
  and and_54 (and_54_out, and_10_out, not_48_out);
  or or_6 (or_6_out, and_54_out, and_55_out);
  and and_55 (and_55_out, and_11_out, not_49_out);
  and and_56 (and_56_out, not_50_out, D);
  and and_57 (and_57_out, and_56_out, not_76_out);
  not not_76 (not_76_out, A);
  and and_58 (and_58_out, D, not_51_out);
  and and_59 (and_59_out, and_58_out, not_77_out);
  not not_77 (not_77_out, A);
  and and_60 (and_60_out, Enable, C);
  or or_7 (or_7_out, A, and_61_out);
  and and_61 (and_61_out, and_12_out, C);
  and and_62 (and_62_out, D, not_78_out);
  not not_78 (not_78_out, C);
  and and_63 (and_63_out, D, B);
  or or_8 (or_8_out, and_63_out, and_64_out);
  and and_64 (and_64_out, Enable, not_52_out);
  and and_65 (and_65_out, Enable, not_79_out);
  not not_79 (not_79_out, B);
  and and_66 (and_66_out, and_13_out, B);
  or or_9 (or_9_out, and_66_out, and_67_out);
  and and_67 (and_67_out, and_14_out, not_53_out);
  and and_68 (and_68_out, not_54_out, B);
  and and_69 (and_69_out, and_68_out, not_80_out);
  not not_80 (not_80_out, A);
  and and_70 (and_70_out, not_55_out, C);
  and and_71 (and_71_out, and_70_out, and_72_out);
  and and_72 (and_72_out, not_56_out, A);
  and and_73 (and_73_out, not_57_out, D);
  and and_74 (and_74_out, and_73_out, not_81_out);
  not not_81 (not_81_out, B);
  and and_75 (and_75_out, and_15_out, and_16_out);
  or or_10 (or_10_out, and_75_out, and_76_out);
  and and_76 (and_76_out, and_17_out, and_18_out);
  and and_77 (and_77_out, Enable, not_58_out);
  and and_78 (and_78_out, and_77_out, not_82_out);
  not not_82 (not_82_out, A);
  and and_79 (and_79_out, Enable, not_59_out);
  and and_80 (and_80_out, and_79_out, B);
  and and_81 (and_81_out, Enable, C);
  and and_82 (and_82_out, and_81_out, not_83_out);
  not not_83 (not_83_out, A);
  and and_83 (and_83_out, and_19_out, not_60_out);
  or or_11 (or_11_out, and_83_out, and_84_out);
  and and_84 (and_84_out, and_20_out, not_61_out);
  and and_85 (and_85_out, not_62_out, D);
  and and_86 (and_86_out, and_85_out, and_87_out);
  and and_87 (and_87_out, not_63_out, not_64_out);
  and and_88 (and_88_out, Enable, not_65_out);
  and and_89 (and_89_out, and_88_out, not_84_out);
  not not_84 (not_84_out, A);
  and and_90 (and_90_out, Enable, C);
  and and_91 (and_91_out, and_90_out, not_85_out);
  not not_85 (not_85_out, A);
  and and_92 (and_92_out, and_21_out, and_22_out);
  or or_12 (or_12_out, and_92_out, and_93_out);
  and and_93 (and_93_out, and_23_out, and_24_out);
  and and_94 (and_94_out, and_25_out, not_66_out);
  or or_13 (or_13_out, and_94_out, and_95_out);
  and and_95 (and_95_out, and_26_out, not_67_out);
  and and_96 (and_96_out, and_27_out, and_28_out);
  or or_14 (or_14_out, and_96_out, and_97_out);
  and and_97 (and_97_out, and_29_out, not_68_out);
  and and_98 (and_98_out, and_30_out, and_31_out);
  or or_15 (or_15_out, and_98_out, and_99_out);
  and and_99 (and_99_out, and_32_out, not_69_out);
  and and_100 (and_100_out, and_33_out, B);
  or or_16 (or_16_out, and_100_out, and_101_out);
  and and_101 (and_101_out, and_34_out, not_70_out);
  and and_102 (and_102_out, and_35_out, not_71_out);
  or or_17 (or_17_out, and_102_out, and_103_out);
  and and_103 (and_103_out, D, not_72_out);
  and and_104 (and_104_out, and_36_out, C);
  or or_18 (or_18_out, and_104_out, and_105_out);
  and and_105 (and_105_out, and_37_out, not_73_out);
  and and_106 (and_106_out, Enable, not_74_out);
  and and_107 (and_107_out, and_106_out, B);
  or or_19 (or_19_out, or_1_out, or_2_out);
  or or_20 (or_20_out, or_3_out, or_4_out);
  or or_21 (or_21_out, or_5_out, and_49_out);
  or or_22 (or_22_out, and_51_out, and_53_out);
  or or_23 (or_23_out, or_6_out, and_57_out);
  or or_24 (or_24_out, and_59_out, and_60_out);
  or or_25 (or_25_out, or_7_out, and_62_out);
  or or_26 (or_26_out, or_8_out, and_65_out);
  or or_27 (or_27_out, or_9_out, and_69_out);
  or or_28 (or_28_out, and_71_out, and_74_out);
  or or_29 (or_29_out, or_10_out, and_78_out);
  or or_30 (or_30_out, and_80_out, and_82_out);
  or or_31 (or_31_out, or_11_out, and_86_out);
  or or_32 (or_32_out, and_89_out, and_91_out);
  or or_33 (or_33_out, or_12_out, or_13_out);
  or or_34 (or_34_out, or_14_out, or_15_out);
  or or_35 (or_35_out, or_16_out, or_17_out);
  or or_36 (or_36_out, or_18_out, and_107_out);
  or or_37 (a1, or_19_out, or_20_out);
  or or_38 (or_38_out, or_21_out, or_22_out);
  or or_39 (or_39_out, or_23_out, or_24_out);
  or or_40 (c1, or_25_out, or_26_out);
  or or_41 (or_41_out, or_27_out, or_28_out);
  or or_42 (or_42_out, or_29_out, or_30_out);
  or or_43 (e1, or_31_out, or_32_out);
  or or_44 (f1, or_33_out, or_34_out);
  or or_45 (g1, or_35_out, or_36_out);
  or or_46 (b1, or_38_out, or_39_out);
  or or_47 (d1, or_41_out, or_42_out);
endmodule

// Zweite / Segemet Ziffer
module Zweite7Segment (
  input  Enable,
  input  D,
  input  C,
  input  B,
  input  A,
  output a2,
  output b2,
  output c2,
  output d2,
  output e2,
  output f2,
  output g2
);

  wire and_1_out, and_2_out, and_3_out, and_4_out, and_5_out, and_6_out, and_7_out, and_8_out, and_9_out,
       and_10_out, and_11_out, and_12_out, and_13_out, and_14_out, and_15_out, not_1_out, not_2_out,
       not_3_out, not_4_out, not_5_out, not_6_out, not_7_out;

  and and_1 (and_1_out, Enable, C);
  and and_2 (and_2_out, Enable, D);
  and and_3 (and_3_out, D, B);
  and and_4 (and_4_out, D, C);
  not not_1 (not_1_out, Enable);
  not not_2 (not_2_out, Enable);
  not not_3 (not_3_out, D);
  not not_4 (not_4_out, C);
  and and_5 (and_5_out, Enable, C);
  and and_6 (and_6_out, Enable, D);
  not not_5 (not_5_out, D);
  not not_6 (not_6_out, C);
  not not_7 (not_7_out, B);
  and and_7 (and_7_out, Enable, C);
  and and_8 (and_8_out, Enable, D);
  or or_1 (a2, and_1_out, and_2_out);
  or or_2 (b2, and_3_out, and_4_out, Enable);
  and and_9 (and_9_out, not_1_out, D, B);
  and and_10 (and_10_out, not_2_out, D, C);
  and and_11 (and_11_out, D, C, B);
  and and_12 (and_12_out, Enable, not_3_out, not_4_out);
  or or_3 (d2, and_5_out, and_6_out);
  and and_13 (and_13_out, Enable, not_5_out, C);
  and and_14 (and_14_out, Enable, D, not_6_out);
  and and_15 (and_15_out, Enable, D, not_7_out);
  or or_4 (g2, and_7_out, and_8_out);
  or or_5 (c2, and_9_out, and_10_out, and_11_out, and_12_out);
  or or_6 (e2, and_13_out, and_14_out, and_15_out);

  assign f2 = 1'b0;
endmodule

module Decoder (
  input  Enable,
  input  D,
  input  C,
  input  B,
  input  A,
  output S1,
  output S2,
  output S3,
  output S4,
  output Z1,
  output Z2,
  output Z3,
  output Z4
);

  wire and_1_out, and_2_out, and_3_out, and_4_out, and_5_out, and_6_out, and_9_out, and_10_out, not_1_out,
       not_2_out, not_3_out, not_4_out, not_5_out, not_6_out, not_7_out, not_8_out;

  not not_1 (not_1_out, D);
  not not_2 (not_2_out, D);
  and and_1 (and_1_out, Enable, D);
  not not_3 (not_3_out, C);
  and and_2 (and_2_out, Enable, D);
  not not_4 (not_4_out, B);
  not not_5 (not_5_out, B);
  and and_3 (and_3_out, Enable, B);
  not not_6 (not_6_out, A);
  and and_4 (and_4_out, Enable, B);
  and and_5 (and_5_out, Enable, not_1_out);
  not not_7 (not_7_out, C);
  and and_6 (and_6_out, Enable, not_2_out);
  and and_7 (S3, and_1_out, not_3_out);
  and and_8 (S4, and_2_out, C);
  and and_9 (and_9_out, Enable, not_4_out);
  not not_8 (not_8_out, A);
  and and_10 (and_10_out, Enable, not_5_out);
  and and_11 (Z3, and_3_out, not_6_out);
  and and_12 (Z4, and_4_out, A);
  and and_13 (S1, and_5_out, not_7_out);
  and and_14 (S2, and_6_out, C);
  and and_15 (Z1, and_9_out, not_8_out);
  and and_16 (Z2, and_10_out, A);
endmodule
